# Fritzing sketch course_led (saved by Fritzing 0.9.3b)
breadboards: 1

parts:
  S1 = Pushbutton [package="[SMD]"]
  Composant1 = Arduino Uno (Rev3) - ICSP
  R1 = Resistor [tolerance=±5% resistance=220 package=THT]
  Composant2 = NeoPixel Stick [part_number=1426]

nets:
  5V: S1.Pin_1, S1.Pin_2, Composant1.5V, R1.Pin_0, Composant2.+5V
  N1: S1.Pin_3, S1.Pin_4, Composant1.D8, R1.Pin_1
  GND: Composant1.GND, Composant2.GND
  N2: Composant1.D4, Composant2.DATAOUT

custom parts:
  NeoPixel Stick: Make your own little LED strip arrangement with this stick of NeoPixel LEDs. We crammed 8 of the tiny 5050 (5mm x 5mm) smart RGB LEDs onto a PCB with mounting holes and a chainable design. Use only one microcontroller pin to control as many as you can chain together! Each LED is addressable as the driver chip is inside the LED. Each one has ~18mA constant current drive so the color will be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
