# Fritzing sketch memo_music (saved by Fritzing 0.9.3b)
breadboards: 1

parts:
  S1 = Pushbutton [package="[THT]"]
  S2 = Pushbutton [package="[THT]"]
  S3 = Pushbutton [package="[THT]"]
  S4 = Pushbutton [package="[THT]"]
  S5 = Pushbutton [package="[THT]"]
  J1 = Piezo Speaker
  R1 = Resistor [tolerance=±5% resistance=220 package="2512 [SMD]"]
  R2 = Resistor [tolerance=±5% resistance=220 package="2512 [SMD]"]
  R3 = Resistor [tolerance=±5% resistance=220 package="2512 [SMD]"]
  R4 = Resistor [tolerance=±5% resistance=220 package="2512 [SMD]"]
  R5 = Resistor [tolerance=±5% resistance=220 package="2512 [SMD]"]
  Composant1 = Arduino Uno (Rev3) - ICSP

nets:
  N1: S1.Pin_1, S1.Pin_2, S2.Pin_1, S2.Pin_2, S3.Pin_1, S3.Pin_2, S4.Pin_1, S4.Pin_2, S5.Pin_1, S5.Pin_2, Composant1.5V
  N2: S1.Pin_3, S1.Pin_4, R5.Pin_1, Composant1.D2
  N3: S2.Pin_3, S2.Pin_4, R4.Pin_1, Composant1.D3_PWM
  N4: S3.Pin_3, S3.Pin_4, R3.Pin_1, Composant1.D4
  N5: S4.Pin_3, S4.Pin_4, R2.Pin_1, Composant1.D7
  N6: S5.Pin_3, S5.Pin_4, R1.Pin_1, Composant1.D8
  N7: J1.pin1, R1.Pin_0, R2.Pin_0, R3.Pin_0, R4.Pin_0, R5.Pin_0, Composant1.GND
  N8: J1.pin2, Composant1.D12/MISO
