# Fritzing sketch ring_pong (saved by Fritzing 0.9.3b)
breadboards: 1

parts:
  S1 = Pushbutton [package="[THT]"]
  S2 = Pushbutton [package="[THT]"]
  C1 = Ceramic Capacitor [capacitance=100nF package="100 mil [THT, multilayer]"]
  C2 = Ceramic Capacitor [capacitance=100nF package="100 mil [THT, multilayer]"]
  Composant2 = 24 NeoPixel Ring [part_number=1586]
  R1 = Resistor [tolerance=±5% resistance=220 package=THT]
  R2 = Resistor [tolerance=±5% resistance=220 package=THT]
  Gizwits_WiFi_Witty_ESP-12F1 = Gizwits WiFi Witty ESP-12F

nets:
  N1: S1.Pin_1, S1.Pin_2, C1.1, R2.Pin_1, Gizwits_WiFi_Witty_ESP-12F1.GPIO5
  GND: S1.Pin_3, S1.Pin_4, S2.Pin_3, S2.Pin_4, C1.0, C2.1, Composant2.GND, R1.Pin_1, R2.Pin_0, Gizwits_WiFi_Witty_ESP-12F1.GND
  N2: S2.Pin_1, S2.Pin_2, C2.0, R1.Pin_0, Gizwits_WiFi_Witty_ESP-12F1.GPIO16
  N3: Composant2.IN, Gizwits_WiFi_Witty_ESP-12F1.GPIO13
  VDD: Composant2.VDD, Gizwits_WiFi_Witty_ESP-12F1.VCC

custom parts:
  24 NeoPixel Ring: 24 ultra bright smart LED NeoPixels are arranged in a circle with 2.6" (66mm) outer diameter. The rings are 'chainable' - connect the output pin of one to the input pin of another. Use only one microcontroller pin to control as many as you can chain together! Each LED is addressable as the driver chip is inside the LED. Each one has ~18mA constant current drive so the color will be very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
